// Digital circuit address.dig as structural Verilog
module address (
  input  A7,
  input  A8,
  input  A9,
  input  A10,
  input  A11,
  input  A12,
  input  A13,
  input  A14,
  input  A15,
  input  A16,
  input  A17,
  input  A18,
  input  A19,
  input  A20,
  input  A21,
  input  A22,
  input  A23,
  output nRAM_EXT,
  output nROM,
  output nIO,
  output nRAM
);

  wire nand_1_out, nand_2_out, nand_3_out, nand_4_out, nand_5_out, or_1_out, or_2_out;

  nand nand_1 (nand_1_out, A15, 1'b1);
  nand nand_2 (nand_2_out, A14, A13, A12, A11, A10, A9, A8, A7);
  nand nand_3 (nand_3_out, A20, A21);
  nand nand_4 (nand_4_out, A22, A23);
  or or_1 (or_1_out, A23, A22, A21, A20, A19, A18, A17, A16);
  nand nand_5 (nand_5_out, nand_1_out, nand_2_out);
  or or_2 (or_2_out, nand_3_out, nand_4_out);
  or or_3 (nRAM_EXT, A19, or_2_out);
  or or_4 (nROM, or_1_out, nand_1_out);
  nand nand_6 (nIO, nand_1_out, ~or_1_out, ~nand_2_out);  // NAnd
  or or_5 (nRAM, or_1_out, nand_5_out);

  // Notes on the sheet:
  //   10.5; 44
  //   10; 30
  //   HC30
  //   AHC00
  //   3*AHC32
  //   3*8.5=25.5
  //   11; 38.5
  //   11.5; 52.5
  //   10; 53
  //   AHC32
  //   13.5; 69.5
  //   12.5; 61
  //   11; 61.5
  //   AHC138
  //   11.5; 69.5
  //   12; 78
  //   11; 81
  //   (11; 41.5 for select bits A4-A6)
  //   Worst case 81ns for I/O chip select
  //   Needs to happen 
  //   10ns before rising edge of clock for 65C22
  //   30ns before rising edge of clock for 65C51
  //   => half-period of clock >= 81+30 = 111ns
  //   => period of clock >= 222ns
  //   => frequency <= 4.50MHz
  //   for the ROM
  //   => half-period of clock >= 23.5+21+70 = 114.5ns
  //   => clock >= 229ns
  //         & clock >= 78+150+21 = 249ns
  //   => frequency <= 4.01Mhz
  //   AHC00: 1; 8.5
  //   AHC32: 1; 8.5
  //   HC30: 0; 23
  //   AHC138 act high: 1; 11.5
  //   AHC138 act low: 1; 11.5
  //   AHC138 select: 1; 11.5
endmodule

/* Test case:
A23 A22 A21 A20 A19 A18 A17 A16 A15 A14 A13 A12 A11 A10 A9 A8 A7   ~ROM ~RAM ~RAM_EXT ~IO
1   0   X   X   X   X   X   X   X   X   X   X   X   X   X  X  X    1    1     1     1
1   1   0   X   X   X   X   X   X   X   X   X   X   X   X  X  X    1    1     1     1
1   1   1   0   X   X   X   X   X   X   X   X   X   X   X  X  X    1    1     1     1
1   1   1   1   0   X   X   X   X   X   X   X   X   X   X  X  X    1    1     0     1
1   1   1   1   1   X   X   X   X   X   X   X   X   X   X  X  X    1    1     1     1
0   1   X   X   X   X   X   X   X   X   X   X   X   X   X  X  X    1    1     1     1
0   0   1   X   X   X   X   X   X   X   X   X   X   X   X  X  X    1    1     1     1
0   0   0   1   X   X   X   X   X   X   X   X   X   X   X  X  X    1    1     1     1
0   0   0   0   0   1   X   X   X   X   X   X   X   X   X  X  X    1    1     1     1
0   0   0   0   0   0   1   X   X   X   X   X   X   X   X  X  X    1    1     1     1
0   0   0   0   0   0   0   1   X   X   X   X   X   X   X  X  X    1    1     1     1
0   0   0   0   0   0   0   0   1   X   X   X   X   X   X  X  X    0    1     1     1
0   0   0   0   0   0   0   0   0   1   1   1   1   1   1  1  1    1    1     1     0
0   0   0   0   0   0   0   0   0   1   1   1   1   1   1  1  0    1    0     1     1
0   0   0   0   0   0   0   0   0   1   1   1   1   1   1  0  X    1    0     1     1
0   0   0   0   0   0   0   0   0   1   1   1   1   1   0  X  X    1    0     1     1
0   0   0   0   0   0   0   0   0   1   1   1   1   0   X  X  X    1    0     1     1
0   0   0   0   0   0   0   0   0   1   1   1   0   X   X  X  X    1    0     1     1
0   0   0   0   0   0   0   0   0   1   1   0   X   X   X  X  X    1    0     1     1
0   0   0   0   0   0   0   0   0   1   0   X   X   X   X  X  X    1    0     1     1
0   0   0   0   0   0   0   0   0   0   X   X   X   X   X  X  X    1    0     1     1
*/
