// Digital circuit pulse.dig as structural Verilog
module pulse (
  input  RnW,
  input  CLK,
  output nRD,
  output nWR
);

  wire not_1_out;

  not not_1 (not_1_out, CLK);
  nand nand_1 (nRD, RnW, RnW);
  or or_1 (nWR, RnW, not_1_out);
endmodule

/* Test case:
CLK R~W  ~RD  ~WR
0   0    1    1
1   0    1    0
0   1    0    1
1   1    0    1
*/
